# Fritzing sketch Sketch (saved by Fritzing 0.9.3b)
circuit board: 8.46667cm x 5.64444cm
breadboards: 2

parts:
  U1 = ESP8266 NodeMCU LoLin module
  Componente1 = Arduino Nano (Rev3.0)
  C1 = Electrolytic Capacitor [capacitance=1mF voltage=10V package="100 mil [THT, electrolytic]"]
  Power_plug1 = Power plug
  DHT1 = Humidity and Temperature Sensor DHT11
  Componente2 = MQ-4
  R1 = Resistor [tolerance=±5% resistance=220 package=THT]

nets:
  GND: U1.GND, Componente1.GND, C1.-, Power_plug1.GND, DHT1.GND_2, Componente2.AO
  N1: U1.D5, DHT1.Data-signal, R1.Pin_1
  N2: U1.RX, Componente1.D1/TX
  N3: U1.TX, Componente1.D0/RX
  VCC: U1.Vin, Componente1.VIN, C1.+, Power_plug1.VCC, DHT1.Vcc, Componente2.VCC, R1.Pin_0
  N4: Componente1.A1, Componente2.GND

custom parts:
  ESP8266 NodeMCU LoLin module: ESP8266 based NodeMCU
  Humidity and Temperature Sensor DHT11: Digital relative humidity & temperature sensor DHT11
